// Logisim project GangeMedTi.circ as structural Verilog: 5 circuits, main circuit Half Adder
module Half_Adder (
  input  X_inn,
  input  Y_inn,
  output Sum,
  output Cout
);

  and and_1 (Cout, X_inn, Y_inn);
  xor xor_1 (Sum, X_inn, Y_inn);
endmodule

module Full_Adder (
  input  X_inn,
  input  Y_inn,
  input  C_inn,
  output Sum,
  output Cout
);

  wire and_1_out, and_2_out, and_3_out, xor_1_out;

  xor xor_1 (xor_1_out, X_inn, Y_inn);
  and and_1 (and_1_out, X_inn, Y_inn);
  and and_2 (and_2_out, X_inn, C_inn);
  and and_3 (and_3_out, C_inn, Y_inn);
  xor xor_2 (Sum, xor_1_out, C_inn);
  or or_1 (Cout, and_1_out, and_2_out, and_3_out);
endmodule

// Mul
module Multiply_10 (
  input  [3:0] Inn,
  output [7:0] Out
);

  wire full_adder_1_cout, half_adder_1_cout, half_adder_2_cout;

  // Probe on Inn
  Half_Adder half_adder_1 (.Sum(Out[3]), .Cout(half_adder_1_cout), .X_inn(Inn[2]), .Y_inn(Inn[0]));
  Full_Adder full_adder_1 (
    .Sum(Out[4]), .Cout(full_adder_1_cout), .X_inn(Inn[3]), .Y_inn(Inn[1]), .C_inn(half_adder_1_cout));
  Half_Adder half_adder_2 (.Sum(Out[5]), .Cout(half_adder_2_cout), .X_inn(Inn[2]), .Y_inn(full_adder_1_cout));
  Half_Adder half_adder_3 (.Sum(Out[6]), .Cout(Out[7]), .X_inn(Inn[3]), .Y_inn(half_adder_2_cout));
  // Probe on {Out[7:3], Inn[1:0], 1'b0}

  assign Out[2:0] = {Inn[1:0], 1'b0};
endmodule

// Neg
module Make_Negative (
  input  Negative,
  input  [7:0] Inn,
  output [8:0] Out
);

  wire half_adder_1_cout, half_adder_2_cout, half_adder_3_cout, half_adder_4_cout, half_adder_5_cout,
       half_adder_6_cout, half_adder_7_cout, half_adder_8_cout, xor_1_out, xor_2_out, xor_3_out, xor_4_out,
       xor_5_out, xor_6_out, xor_7_out, xor_8_out;

  // Probe on Inn
  xor xor_1 (xor_1_out, Negative, Inn[0]);
  xor xor_2 (xor_2_out, Negative, Inn[4]);
  xor xor_3 (xor_3_out, Negative, Inn[1]);
  xor xor_4 (xor_4_out, Negative, Inn[5]);
  xor xor_5 (xor_5_out, Negative, Inn[2]);
  xor xor_6 (xor_6_out, Negative, Inn[3]);
  xor xor_7 (xor_7_out, Negative, Inn[6]);
  xor xor_8 (xor_8_out, Negative, Inn[7]);
  Half_Adder half_adder_1 (.Sum(Out[0]), .Cout(half_adder_1_cout), .X_inn(xor_1_out), .Y_inn(Negative));
  Half_Adder half_adder_2 (.Sum(Out[1]), .Cout(half_adder_2_cout), .X_inn(xor_3_out), .Y_inn(half_adder_1_cout));
  Half_Adder half_adder_3 (.Sum(Out[2]), .Cout(half_adder_3_cout), .X_inn(xor_5_out), .Y_inn(half_adder_2_cout));
  Half_Adder half_adder_4 (.Sum(Out[3]), .Cout(half_adder_4_cout), .X_inn(xor_6_out), .Y_inn(half_adder_3_cout));
  Half_Adder half_adder_5 (.Sum(Out[4]), .Cout(half_adder_5_cout), .X_inn(xor_2_out), .Y_inn(half_adder_4_cout));
  Half_Adder half_adder_6 (.Sum(Out[5]), .Cout(half_adder_6_cout), .X_inn(xor_4_out), .Y_inn(half_adder_5_cout));
  Half_Adder half_adder_7 (.Sum(Out[6]), .Cout(half_adder_7_cout), .X_inn(xor_7_out), .Y_inn(half_adder_6_cout));
  Half_Adder half_adder_8 (.Sum(Out[7]), .Cout(half_adder_8_cout), .X_inn(xor_8_out), .Y_inn(half_adder_7_cout));
  // Probe on {Negative, Out[7:0]}

  assign Out[8] = Negative;
  // also tied to GND on the sheet: half_adder_8_cout
endmodule

module Main_Circuit (
  input  in_1,
  input  [3:0] in_2,
  output [8:0] out_3
);

  wire [7:0] multiply_10_1_out;

  // Probe on in_2
  Multiply_10 multiply_10_1 (.Inn(in_2), .Out(multiply_10_1_out));
  // Probe on multiply_10_1_out
  Make_Negative make_negative_1 (.Negative(in_1), .Inn(multiply_10_1_out), .Out(out_3));
  // Probe on out_3
endmodule
