// Logisim project Oblig2.circ as structural Verilog
// Count
module Counter (
  input  Clock,
  input  Reset,
  output [3:0] Out
);

  wire adder_1_cout, not_1_out;
  wire [3:0] adder_1_out;

  not not_1 (not_1_out, adder_1_cout);
  Register #(.width(4)) register_1 (.D(adder_1_out), .en(not_1_out), .Q(Out), .clk(Clock), .clr(Reset));
  Adder #(.width(4)) adder_1 (.a(Out), .b(4'b0001), .out(adder_1_out), .cout(adder_1_cout));  // open: cin
endmodule

module RAM_Module (
  input  [7:0] in_1,
  input  in_2,
  input  in_3,
  input  in_4,
  output [7:0] out_5
);

  wire clock_1_out, not_1_out, R_out;
  wire [3:0] counter_1_out;
  wire [7:0] ram_1_data;

  Clock clock_1 (.out(clock_1_out));
  Counter counter_1 (.Clock(clock_1_out), .Reset(R_out), .Out(counter_1_out));
  Button R (.out(R_out));
  _4_bit_Tri_state_Buffer u_4_bit_tri_state_buffer_1 ();  // open: Inn_1, Inn_2, Enable_1, Enable_2, Out_1, Out_2
  _4_bit_Tri_state_Buffer u_4_bit_tri_state_buffer_2 ();  // open: Inn_1, Inn_2, Enable_1, Enable_2, Out_1, Out_2
  RAM #(.addrWidth(4), .bus("asynch")) ram_1 (
    .addr(counter_1_out), .data(ram_1_data), .sel(in_2), .ld(in_4), .clr(in_3));
  assign out_5 = in_4 ? ram_1_data : 8'bz;  // Controlled_Buffer controlled_buffer_1
  assign ram_1_data = not_1_out ? in_1 : 8'bz;  // Controlled_Buffer controlled_buffer_2
  not not_1 (not_1_out, in_4);
  Register CPU_R ();  // open: D, en, Q, clk, clr
endmodule

module _4_bit_Tri_state_Buffer (
  input  Enable_1,
  input  [3:0] Inn_1,
  input  [3:0] Inn_2,
  input  Enable_2,
  output [3:0] Out_1,
  output [3:0] Out_2
);

  wire clock_1_out;
  wire [3:0] register_1_q, register_2_q;

  Register #(.width(4)) register_1 (.D(Inn_1), .Q(register_1_q), .clk(clock_1_out));  // open: en, clr
  Register #(.width(4)) register_2 (.D(Inn_2), .Q(register_2_q), .clk(clock_1_out));  // open: en, clr
  Clock clock_1 (.out(clock_1_out));
  assign Out_1 = Enable_1 ? register_1_q : 4'bz;  // Controlled_Buffer controlled_buffer_1
  assign Out_2 = Enable_2 ? register_2_q : 4'bz;  // Controlled_Buffer controlled_buffer_2
endmodule
